# Fritzing sketch circuit (saved by Fritzing 0.9.3b)
circuit board: 18.2719cm x 8.35194cm
breadboards: 1

parts:
  R2 = Resistor [tolerance=±5% resistance=10k package=THT]
  Bauteil1 = Arduino Micro (Rev3)
  LED1 = LED - 5mm [color="Red (633nm)" part_number="Display Licht" package="5 mm [THT]"]
  R_LCD = Resistor [tolerance=±5% resistance=100 package=THT]
  C1 = Electrolytic Capacitor [capacitance=220µF voltage=50V package="200 mil [THT, electrolytic]"]
  R1 = Resistor [tolerance=±5% resistance=1.2k package=THT]
  D5 = Diode [package=diode-1n4001]
  J2 = female pin header, 2 pins [form="♀ (female)"]
  D1 = Diode [package=diode-1n4001]
  D4 = Diode [package=diode-1n4001]
  C2 = Electrolytic Capacitor [capacitance=220µF voltage=50V package="200 mil [THT, electrolytic]"]
  D2 = Diode [package=diode-1n4001]
  D3 = Diode [package=diode-1n4001]
  U2 = Voltage Regulator - 5V [part_number="3,3 Volt Regulator" package="TO220 [THT]"]
  S1 = Pushbutton [package="[THT]"]
  S2 = Pushbutton [package="[THT]"]
  R3 = Resistor [tolerance=±5% resistance=10k package=THT]
  R4 = Resistor [tolerance=±5% resistance=10k package=THT]
  U3 = LCD-16X2 [part_number=LCD package=lcd-8x2]
  U4 = Sharp PC817 [package=THT]

nets:
  VIN: R2.Pin_0, Bauteil1.VIN, U2.output_voltage, R3.Pin_0, R4.Pin_0, U3.VDD
  N1: R2.Pin_1, Bauteil1.D2/SDA, U4.Pin_4
  N2: Bauteil1.MOSI, U3.R_W
  N3: Bauteil1.RXLED/SS, U3.VSS
  GND: Bauteil1.GND, D4.A, C2.-, D2.A, U2.GND, S1.Pin_2, S2.Pin_1, S2.Pin_2, U4.Pin_3
  N4: Bauteil1.D7, S1.Pin_4, R3.Pin_1
  N5: Bauteil1.D8_PWM/A8, S2.Pin_3, S2.Pin_4, R4.Pin_1
  N6: Bauteil1.D9_PWM/A9, R_LCD.Pin_1
  N7: Bauteil1.SCK, U3.VO
  N8: Bauteil1.MISO, U3.RS
  N9: LED1.cathode, U3.E
  N10: LED1.anode, R_LCD.Pin_0
  N11: C1.-, D5.A, J2.pin1, D4.C, C2.+, D3.A, U4.Pin_2
  N12: C1.+, D1.C, D3.C, U2.input_voltage
  N13: R1.Pin_0, J2.pin2, D1.A, D2.C
  N14: R1.Pin_1, D5.C, U4.Pin_1
